# Fritzing sketch ESP8266 ir-thermostat (saved by Fritzing 0.9.3b)
breadboards: 1

parts:
  U1 = NodeMCU V1.0
  Part1 = LCD1602-I2C
  S1 = Momentary Switch [package=ksa_sealed_tac_switch]
  S2 = Momentary Switch [package=ksa_sealed_tac_switch]
  S3 = Momentary Switch [package=ksa_sealed_tac_switch]
  R1 = Resistor [tolerance=±1% resistance=10 package=THT]
  R2 = Resistor [tolerance=±1% resistance=10 package=THT]
  R3 = Resistor [tolerance=±1% resistance=10 package=THT]

nets (from the breadboard view):
  N1: U1.D0, S1.1, R1.Pin_1
  N2: U1.D1, Part1.SCL
  N3: U1.D2, Part1.SDA
  N4: U1.3V3, S2.3, S3.3
  GND: U1.GND, Part1.GND, S1.3, R1.Pin_0, R2.Pin_0, R3.Pin_0
  N5: U1.D5, S3.1, R3.Pin_1
  N6: U1.D6, S2.1, R2.Pin_1
  VIN: U1.Vin, Part1.VCC

custom parts:
  NodeMCU V1.0: ESP8266 based NodeMCU
  LCD1602-I2C: A standard character display, usually with 2x16 characters. Comes in many colors with LCM1602 IIC attached.
